// Logisim project RegisterChris.circ as structural Verilog: 1 circuit, main circuit main
module main (
  input  [15:0] Data,
  input  Clock,
  input  Write_Enable,
  input  [3:0] rs,
  input  [3:0] rt,
  input  [3:0] rd,
  output [15:0] out_7,
  output [15:0] out_8,
  output [15:0] out_9
);

  wire and_1_out, and_2_out, and_3_out, and_4_out, and_5_out, and_6_out, and_7_out, and_8_out, and_9_out,
       and_10_out, and_11_out, and_12_out, and_13_out, and_14_out, and_15_out, and_16_out, and_17_out,
       demultiplexer_1_out0, demultiplexer_1_out1, demultiplexer_1_out2, demultiplexer_1_out3,
       demultiplexer_1_out4, demultiplexer_1_out5, demultiplexer_1_out6, demultiplexer_1_out7,
       demultiplexer_1_out8, demultiplexer_1_out9, demultiplexer_1_out10, demultiplexer_1_out11,
       demultiplexer_1_out12, demultiplexer_1_out13, demultiplexer_1_out14, demultiplexer_1_out15;
  wire [15:0] register_1_q, register_2_q, register_3_q, register_4_q, register_5_q, register_6_q,
       register_7_q, register_8_q, register_9_q, register_10_q, register_11_q, register_12_q, register_13_q,
       register_14_q, register_15_q, register_16_q;

  Demultiplexer #(.select(4), .enable("false")) demultiplexer_1 (
    .out0(demultiplexer_1_out0), .out1(demultiplexer_1_out1), .out2(demultiplexer_1_out2),
    .out3(demultiplexer_1_out3), .out4(demultiplexer_1_out4), .out5(demultiplexer_1_out5),
    .out6(demultiplexer_1_out6), .out7(demultiplexer_1_out7), .out8(demultiplexer_1_out8),
    .out9(demultiplexer_1_out9), .out10(demultiplexer_1_out10), .out11(demultiplexer_1_out11),
    .out12(demultiplexer_1_out12), .out13(demultiplexer_1_out13), .out14(demultiplexer_1_out14),
    .out15(demultiplexer_1_out15), .in(1'b1), .sel(rd));
  and and_1 (and_1_out, Clock, Write_Enable);
  and and_2 (and_2_out, and_1_out, demultiplexer_1_out0);
  and and_3 (and_3_out, and_1_out, demultiplexer_1_out1);
  and and_4 (and_4_out, and_1_out, demultiplexer_1_out2);
  and and_5 (and_5_out, and_1_out, demultiplexer_1_out3);
  and and_6 (and_6_out, and_1_out, demultiplexer_1_out4);
  and and_7 (and_7_out, and_1_out, demultiplexer_1_out5);
  and and_8 (and_8_out, and_1_out, demultiplexer_1_out6);
  and and_9 (and_9_out, and_1_out, demultiplexer_1_out7);
  and and_10 (and_10_out, and_1_out, demultiplexer_1_out8);
  and and_11 (and_11_out, and_1_out, demultiplexer_1_out9);
  and and_12 (and_12_out, and_1_out, demultiplexer_1_out10);
  and and_13 (and_13_out, and_1_out, demultiplexer_1_out11);
  and and_14 (and_14_out, and_1_out, demultiplexer_1_out12);
  and and_15 (and_15_out, and_1_out, demultiplexer_1_out13);
  and and_16 (and_16_out, and_1_out, demultiplexer_1_out14);
  and and_17 (and_17_out, and_1_out, demultiplexer_1_out15);
  Register #(.width(16)) register_1 (.D(Data), .Q(register_1_q), .clk(and_2_out));  // open: en, clr
  Register #(.width(16)) register_2 (.D(Data), .Q(register_2_q), .clk(and_3_out));  // open: en, clr
  Register #(.width(16)) register_3 (.D(Data), .Q(register_3_q), .clk(and_4_out));  // open: en, clr
  Register #(.width(16)) register_4 (.D(Data), .Q(register_4_q), .clk(and_5_out));  // open: en, clr
  Register #(.width(16)) register_5 (.D(Data), .Q(register_5_q), .clk(and_6_out));  // open: en, clr
  Register #(.width(16)) register_6 (.D(Data), .Q(register_6_q), .clk(and_7_out));  // open: en, clr
  Register #(.width(16)) register_7 (.D(Data), .Q(register_7_q), .clk(and_8_out));  // open: en, clr
  Register #(.width(16)) register_8 (.D(Data), .Q(register_8_q), .clk(and_9_out));  // open: en, clr
  Register #(.width(16)) register_9 (.D(Data), .Q(register_9_q), .clk(and_10_out));  // open: en, clr
  Register #(.width(16)) register_10 (.D(Data), .Q(register_10_q), .clk(and_11_out));  // open: en, clr
  Register #(.width(16)) register_11 (.D(Data), .Q(register_11_q), .clk(and_12_out));  // open: en, clr
  Register #(.width(16)) register_12 (.D(Data), .Q(register_12_q), .clk(and_13_out));  // open: en, clr
  Register #(.width(16)) register_13 (.D(Data), .Q(register_13_q), .clk(and_14_out));  // open: en, clr
  Register #(.width(16)) register_14 (.D(Data), .Q(register_14_q), .clk(and_15_out));  // open: en, clr
  Register #(.width(16)) register_15 (.D(Data), .Q(register_15_q), .clk(and_16_out));  // open: en, clr
  Register #(.width(16)) register_16 (.D(Data), .Q(register_16_q), .clk(and_17_out));  // open: en, clr
  Multiplexer #(.select(4), .width(16), .enable("false")) multiplexer_1 (
    .in0(register_1_q), .in1(register_2_q), .in2(register_3_q), .in3(register_4_q), .in4(register_5_q),
    .in5(register_6_q), .in6(register_7_q), .in7(register_8_q), .in8(register_9_q), .in9(register_10_q),
    .in10(register_11_q), .in11(register_12_q), .in12(register_13_q), .in13(register_14_q),
    .in14(register_15_q), .in15(register_16_q), .out(out_7), .sel(rs));
  Multiplexer #(.select(4), .width(16), .enable("false")) multiplexer_2 (
    .in0(register_1_q), .in1(register_2_q), .in2(register_3_q), .in3(register_4_q), .in4(register_5_q),
    .in5(register_6_q), .in6(register_7_q), .in7(register_8_q), .in8(register_9_q), .in9(register_10_q),
    .in10(register_11_q), .in11(register_12_q), .in12(register_13_q), .in13(register_14_q),
    .in14(register_15_q), .in15(register_16_q), .out(out_8), .sel(rt));
  Multiplexer #(.select(4), .width(16), .enable("false")) multiplexer_3 (
    .in0(register_1_q), .in1(register_2_q), .in2(register_3_q), .in3(register_4_q), .in4(register_5_q),
    .in5(register_6_q), .in6(register_7_q), .in7(register_8_q), .in8(register_9_q), .in9(register_10_q),
    .in10(register_11_q), .in11(register_12_q), .in12(register_13_q), .in13(register_14_q),
    .in14(register_15_q), .in15(register_16_q), .out(out_9), .sel(rd));
endmodule
