// Logisim project completeCPU.circ as structural Verilog: 1 circuit, main circuit main
module main (
);

  wire alucris_1_p4, clock_1_out, tabla_control_1_alusrcabajo, tabla_control_1_memread,
       tabla_control_1_memtoreg, tabla_control_1_memwrite, tabla_control_1_regwrite;
  wire [1:0] tabla_control_1_pcsrc;
  wire [3:0] ram_1_data_2, tabla_control_1_alu_operation;
  wire [11:4] ram_1_data;
  wire [15:0] adder_1_out, alucris_1_p5, bit_extender_1_out, bit_extender_2_out, main_1_out_7, main_1_out_8,
       main_1_out_9, multiplexer_1_out, multiplexer_2_out, multiplexer_3_out, multiplexer_4_out,
       multiplexer_5_out, multiplexer_6_out, ram_2_data, register_1_q;
  wire [15:12] ram_1_data_3;

  Register #(.width(16), .trigger("falling")) register_1 (
    .D(adder_1_out), .Q(register_1_q), .clk(clock_1_out));  // open: en, clr
  Adder #(.width(16)) adder_1 (.a(register_1_q), .b(multiplexer_1_out), .out(adder_1_out));  // open: cin, cout
  Multiplexer #(.select(2), .width(16), .enable("false")) multiplexer_1 (
    .in0(16'h1), .in1(multiplexer_2_out), .in2(multiplexer_3_out), .in3(bit_extender_1_out),
    .out(multiplexer_1_out), .sel(tabla_control_1_pcsrc));
  Clock clock_1 (.out(clock_1_out));
  RAM #(.addrWidth(16), .dataWidth(16)) ram_1 (
    .addr(register_1_q), .data({ram_1_data_3, ram_1_data_2, ram_1_data}), .clk(clock_1_out));  // open: sel, ld, clr
  assign bit_extender_1_out = {{4{ram_1_data[11]}}, {ram_1_data, ram_1_data_2}};  // Bit_Extender bit_extender_1
  Multiplexer #(.width(16), .enable("false")) multiplexer_2 (
    .in0(16'h1), .in1(bit_extender_2_out), .out(multiplexer_2_out), .sel(alucris_1_p4));
  Tabla_control tabla_control_1 (
    .Operation(ram_1_data_3), .Alu_Operation(tabla_control_1_alu_operation),
    .MemRead(tabla_control_1_memread), .MemWrite(tabla_control_1_memwrite),
    .MemtoReg(tabla_control_1_memtoreg), .RegWrite(tabla_control_1_regwrite),
    .AluSrcAbajo(tabla_control_1_alusrcabajo), .PCSrc(tabla_control_1_pcsrc));  // open: Branch, RegDest
  Multiplexer #(.width(16), .enable("false")) multiplexer_3 (
    .in0(bit_extender_2_out), .in1(16'h1), .out(multiplexer_3_out), .sel(alucris_1_p4));
  RegisterChris_main main_1 (
    .Data(multiplexer_6_out), .Clock(clock_1_out), .Write_Enable(tabla_control_1_regwrite),
    .rd(ram_1_data_2), .rs(ram_1_data[7:4]), .rt(ram_1_data[11:8]), .out_7(main_1_out_7),
    .out_8(main_1_out_8), .out_9(main_1_out_9));
  assign bit_extender_2_out = {{8{ram_1_data[11]}}, ram_1_data};  // Bit_Extender bit_extender_2
  Multiplexer #(.width(16), .enable("false")) multiplexer_4 (
    .in0(main_1_out_7), .in1(main_1_out_9), .out(multiplexer_4_out), .sel(tabla_control_1_alusrcabajo));
  Multiplexer #(.width(16), .enable("false")) multiplexer_5 (
    .in0(main_1_out_8), .in1(bit_extender_2_out), .out(multiplexer_5_out), .sel(tabla_control_1_alusrcabajo));
  Multiplexer #(.width(16), .enable("false")) multiplexer_6 (
    .in0(alucris_1_p5), .in1(ram_2_data), .out(multiplexer_6_out), .sel(tabla_control_1_memtoreg));
  // AluCris alucris_1: pin names not known; wires that end beside it: multiplexer_4_out, multiplexer_5_out, tabla_control_1_alu_operation, alucris_1_p4, alucris_1_p5
  RAM #(.addrWidth(16), .dataWidth(16), .bus("separate")) ram_2 (
    .addr(alucris_1_p5), .din(main_1_out_9), .data(ram_2_data), .str(tabla_control_1_memwrite),
    .clk(clock_1_out), .ld(tabla_control_1_memread));  // open: sel, clr
endmodule
