// Logisim project controlCris.circ as structural Verilog: 1 circuit, main circuit Tabla control
module Tabla_control (
  input  [3:0] Operation,
  output [3:0] Alu_Operation,
  output Branch,
  output MemRead,
  output MemWrite,
  output MemtoReg,
  output RegWrite,
  output RegDest,
  output AluSrcAbajo,
  output [1:0] PCSrc
);

  ROM #(.addrWidth(4), .dataWidth(13)) rom_1 (
    .addr(Operation),
    .data({PCSrc, AluSrcAbajo, RegDest, RegWrite, MemtoReg, MemWrite, MemRead, Branch, Alu_Operation}));  // open: sel

  // Notes on the sheet:
  //   PcSrc
  //   00: PC+1
  //   01: BZ
  //   10: BNZ
  //   11: Jump
  //   2. AluOp2
  //   3. AluOp3
  //   4. AluOp4
  //   5. Branch
  //   6. MemRead
  //   7. MemWrite
  //   contents of rom_1 (hex, n*v repeats v):
  //   302 303 1a2 42 301 300 304 0 702 7ff c10 1410 0 0 0 1810
  //   From right to left:
  //   1. AluOp1
  //   10. RegDst
  //   11. AluSrcAbajo
  //   12. PCSrc
  //   13. PCSrc
  //   8. MemtoReg
  //   9. RegWrite
endmodule
